# Fritzing sketch Esquemático (saved by Fritzing 0.9.3b)
breadboards: 1

parts:
  Grove1 = Grove OLED 128x96
  S1 = Pushbutton [package="[SMD]"]
  S2 = Pushbutton [package="[SMD]"]
  S3 = Pushbutton [package="[SMD]"]
  Componente2 = Arduino Nano (Rev3.0)
  R1 = Resistor [tolerance=±5% resistance=220 package="2010 [SMD]"]
  R2 = Resistor [tolerance=±5% resistance=220 package="2010 [SMD]"]
  R3 = Resistor [tolerance=±5% resistance=220 package="2010 [SMD]"]
  J1 = Piezo Speaker
  ZS-042_RTC1 = ZS-042 RTC Module

nets:
  N1: Grove1.SDA, Componente2.A5, ZS-042_RTC1.SDA
  N2: Grove1.SCL, Componente2.A4, ZS-042_RTC1.SCL
  5V: S1.Pin_1, S1.Pin_2, S2.Pin_1, S2.Pin_2, S3.Pin_1, S3.Pin_2, Componente2.5V, ZS-042_RTC1.VCC
  N3: S1.Pin_3, S1.Pin_4, Componente2.D9, R2.Pin_0
  N4: S2.Pin_3, S2.Pin_4, Componente2.D10, R3.Pin_0
  N5: S3.Pin_3, S3.Pin_4, Componente2.D8, R1.Pin_0
  GND: Componente2.GND, R1.Pin_1, R2.Pin_1, R3.Pin_1, J1.pin1, ZS-042_RTC1.GND
  N6: Componente2.D6, J1.pin2
